# Fritzing sketch ESP32-Devkit-v1-30pin (saved by Fritzing 0.9.4)

parts:
  Part3 = Waveshare 4.2" 400×300 ePaper Display Module
  Part4 = BME280 Breakout
  U1 = ESP32 DEVKIT V1 DOIT [part_number=ESP32S-HiLetgo]

nets:
  N1: Part3.VCC, U1.3.3
  GND: Part3.GND, Part4.GND, U1.GND
  N2: Part3.DIN, U1.GPIO23
  N3: Part3.CLK, U1.GPIO18
  N4: Part3.CS, U1.GPIO5
  N5: Part3.DC, U1.GPIO17
  N6: Part3.RST, U1.GPIO16
  N7: Part3.BUSY, U1.GPIO15
  N8: Part4.VCC, U1.GPIO13
  N9: Part4.SCL, U1.GPIO22
  N10: Part4.SDA, U1.GPIO21

custom parts:
  BME280 Breakout: SparkFun Atmospheric Sensor Breakout - BME280 SEN-13676 The SparkFun BME280 Atmospheric Sensor Breakout is the easy way to measure barometric pressure, humidity, and temperature readings all without taking up too much space. Basically, anything you need to know about atmospheric conditions you can find out from this tiny breakout. The BME280 Breakout has been design to be used in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
  ESP32 DEVKIT V1 DOIT: 30GPIO Version
